// Logisim project gigatron.circ as structural Verilog: 1 circuit, main circuit main
module main (
  input  in_1,
  input  in_2,
  input  in_3,
  input  in_4,
  input  in_5,
  input  in_6,
  input  in_7,
  input  in_8,
  input  in_9,
  input  in_10,
  input  in_11,
  input  in_12,
  input  in_13,
  input  in_14,
  input  in_15,
  input  in_16,
  input  in_17,
  input  in_18,
  input  in_19,
  input  in_20,
  input  in_21,
  input  in_22,
  input  in_23,
  input  in_24,
  input  in_25,
  input  in_26,
  input  in_27,
  input  in_28,
  input  in_29,
  input  in_30,
  input  in_31,
  input  in_32,
  input  in_33,
  input  in_34,
  input  in_35,
  input  in_36,
  input  in_37,
  input  in_38,
  input  in_39,
  input  in_40,
  input  in_41,
  input  in_42,
  input  in_43,
  input  in_44,
  input  in_45,
  input  in_46,
  input  in_47,
  input  in_48,
  input  in_49,
  input  in_50,
  input  in_51,
  input  in_52,
  input  in_53,
  input  in_54,
  input  in_55,
  input  in_56,
  input  in_57,
  input  in_58,
  input  in_59,
  input  in_60,
  input  in_61,
  input  in_62,
  input  in_63,
  input  in_64,
  input  in_65,
  input  in_66,
  input  in_67,
  input  in_68,
  input  in_69,
  input  in_70,
  input  in_71,
  input  in_72,
  input  in_73,
  input  in_74,
  input  in_75,
  input  in_76,
  input  in_77,
  input  in_78,
  input  in_79,
  input  in_80,
  input  in_81,
  input  in_82,
  input  in_83,
  input  in_84,
  input  in_85,
  input  in_86,
  input  in_87,
  input  in_88,
  input  in_89,
  input  in_90,
  input  in_91,
  input  in_92,
  input  in_93,
  input  in_94,
  input  in_95,
  input  in_96,
  input  in_97,
  input  in_98,
  input  in_99,
  input  in_100,
  input  in_101,
  input  in_102,
  input  in_103,
  input  in_104,
  input  in_105,
  input  in_106,
  input  in_107,
  input  in_108,
  input  in_109,
  input  in_110
);

  wire AC0, AC1, AC2, AC3, AC4, AC5, AC6, AC7, AE, AL, ALU0, ALU1, ALU2, ALU3, ALU4, ALU5, ALU6, ALU7,
       and_2_out, and_3_out, and_4_out, and_5_out, and_6_out, and_7_out, and_8_out, and_12_out, AR0, AR1,
       AR2, AR3, BUS0, BUS1, BUS2, BUS3, BUS4, BUS5, BUS6, BUS7, button_1_out, CLK1, CLK2, CO, D0, D1, D2,
       D3, D4, D5, D6, D7, DE, EH, EL, IE, IR0, IR1, IR2, IR3, IR4, IR5, IR6, IR7, IX, LD, n74138_1_pin7,
       n74138_1_pin9, n74138_1_pin10, n74138_1_pin11, n74138_1_pin12, n74138_1_pin13, n74138_1_pin14,
       n74138_1_pin15, n74138_2_pin7, n74138_2_pin9, n74138_2_pin12, n74138_2_pin13, n74138_2_pin14,
       n74138_2_pin15, n74139_2_pin4, n74153_1_pin7, n74153_1_pin9, n74153_2_pin7, n74153_2_pin9,
       n74153_3_pin7, n74153_3_pin9, n74153_4_pin7, n74153_4_pin9, n74153_5_pin7, n74153_5_pin9,
       n74153_6_pin7, n74153_6_pin9, n74153_7_pin7, n74153_7_pin9, n74153_8_pin7, n74153_8_pin9,
       n74153_9_pin7, n74153_9_pin9, n74161_1_pin15, n74161_2_pin15, n74161_3_pin15, n74161_4_pin15,
       n74161_5_pin15, n74161_6_pin2, n74161_6_pin15, n74161_9_pin10, n74240_1_pin7, n74240_1_pin8,
       n74240_1_pin9, n74240_1_pin11, n74240_1_pin12, n74240_1_pin13, n74283_1_pin9, not_2_out, not_3_out,
       not_5_out, not_6_out, not_8_out, not_9_out, not_11_out, OE, OL, OUT0, OUT1, OUT2, OUT3, OUT4, OUT5,
       OUT6, OUT7, PC0, PC1, PC2, PC3, PC4, PC5, PC6, PC7, PC8, PC9, PC10, PC11, PC12, PC13, PC14, PC15, PH,
       PL, ROM0, ROM1, ROM2, ROM3, ROM4, ROM5, ROM6, ROM7, ROM8, ROM9, ROM10, ROM11, ROM12, ROM13, ROM14,
       ROM15, RST, shift_register_1_p14, shift_register_1_p15, shift_register_1_p16, shift_register_1_p17,
       shift_register_1_p18, shift_register_1_p19, shift_register_1_p20, shift_register_1_p21, WE, X0, X1,
       X2, X3, X4, X5, X6, X7, XL, Y0, Y1, Y2, Y3, Y4, Y5, Y6, Y7, YL;
  wire [7:0] n74161_5_pin14, n74161_6_pin14, ram_1_dout;
  wire [15:0] n74157_2_pin9;

  Clock clock_1 (.out(CLK1));
  _74138 #(.ShowInternalStructure("true")) u_74138_1 (
    .pin1(IR5), .pin2(IR6), .pin3(IR7), .pin4(in_32), .pin5(in_32), .pin6(in_33), .pin7(n74138_1_pin7),
    .pin15(n74138_1_pin15), .pin14(n74138_1_pin14), .pin13(n74138_1_pin13), .pin12(n74138_1_pin12),
    .pin11(n74138_1_pin11), .pin10(n74138_1_pin10), .pin9(n74138_1_pin9));
  not not_1 (RST, button_1_out);
  Button button_1 (.out(button_1_out));
  _74139 #(.ShowInternalStructure("true")) u_74139_1 (
    .pin1(in_27), .pin2(IR0), .pin3(IR1), .pin4(DE), .pin5(OE), .pin6(AE), .pin7(IE));  // open: pin15, pin14, pin13, pin12, pin11, pin10, pin9
  _74138 #(.ShowInternalStructure("true")) u_74138_2 (
    .pin1(IR2), .pin2(IR3), .pin3(IR4), .pin4(in_31), .pin5(in_31), .pin6(n74138_1_pin7),
    .pin7(n74138_2_pin7), .pin15(n74138_2_pin15), .pin14(n74138_2_pin14), .pin13(n74138_2_pin13),
    .pin12(n74138_2_pin12), .pin11(XL), .pin10(YL), .pin9(n74138_2_pin9));
  _74157 #(.ShowInternalStructure("true")) u_74157_1 (
    .pin1(EL), .pin2(X4), .pin3(D4), .pin4(n74157_2_pin9[4]), .pin5(X5), .pin6(D5), .pin7(n74157_2_pin9[5]),
    .pin15(in_50), .pin14(X6), .pin13(D6), .pin12(n74157_2_pin9[6]), .pin11(X7), .pin10(D7),
    .pin9(n74157_2_pin9[7]));
  _74157 #(.ShowInternalStructure("true")) u_74157_2 (
    .pin1(EL), .pin2(X1), .pin3(D1), .pin4(n74157_2_pin9[1]), .pin5(X2), .pin6(D2), .pin7(n74157_2_pin9[2]),
    .pin15(in_51), .pin14(X3), .pin13(D3), .pin12(n74157_2_pin9[3]), .pin11(X0), .pin10(D0),
    .pin9(n74157_2_pin9[0]));
  _74157 #(.ShowInternalStructure("true")) u_74157_3 (
    .pin1(in_81), .pin2(Y5), .pin3(in_77), .pin4(n74157_2_pin9[13]), .pin5(Y6), .pin6(in_78),
    .pin7(n74157_2_pin9[14]), .pin15(EH), .pin14(Y3), .pin13(in_80), .pin12(n74157_2_pin9[11]), .pin11(Y1),
    .pin10(in_79), .pin9(n74157_2_pin9[9]));
  _74157 #(.ShowInternalStructure("true")) u_74157_4 (
    .pin1(in_104), .pin2(Y0), .pin3(in_100), .pin4(n74157_2_pin9[8]), .pin5(Y7), .pin6(in_101),
    .pin7(n74157_2_pin9[15]), .pin15(EH), .pin14(Y2), .pin13(in_103), .pin12(n74157_2_pin9[10]), .pin11(Y4),
    .pin10(in_102), .pin9(n74157_2_pin9[12]));
  not not_2 (not_2_out, CLK1);
  not not_3 (not_3_out, CLK1);
  // AND_Gate and_1 has open pins: in0=CLK1, in1=not_2_out, out=open
  _74161 #(.ShowInternalStructure("true")) u_74161_1 (
    .pin1(RST), .pin2(CLK1), .pin3(BUS0), .pin4(BUS1), .pin5(BUS2), .pin6(BUS3), .pin7(in_13),
    .pin15(n74161_1_pin15), .pin14(PC0), .pin13(PC1), .pin12(PC2), .pin11(PC3), .pin10(in_13), .pin9(PL));
  not not_4 (CLK2, not_3_out);
  ROM #(.addrWidth(16), .dataWidth(16)) rom_1 (
    .addr({PC15, PC14, PC13, PC12, PC11, PC10, PC9, PC8, PC7, PC6, PC5, PC4, PC3, PC2, PC1, PC0}),
    .data({ROM15, ROM14, ROM13, ROM12, ROM11, ROM10, ROM9, ROM8, ROM7, ROM6, ROM5, ROM4, ROM3, ROM2, ROM1, ROM0}));
  or or_1 (WE, n74138_1_pin9, CLK1);
  and and_2 (and_2_out, n74138_1_pin10, n74138_1_pin7);
  and and_3 (and_3_out, n74138_1_pin13, n74138_1_pin12, n74138_1_pin10);
  and and_4 (and_4_out, n74138_1_pin15, n74138_1_pin13, n74138_1_pin12, n74138_1_pin11, n74138_1_pin7);
  and and_5 (and_5_out, n74138_1_pin15, n74138_1_pin14, n74138_1_pin13, n74138_1_pin11);
  and and_6 (and_6_out, n74138_1_pin7, IR7);
  _74240 #(.ShowInternalStructure("true")) u_74240_1 (
    .pin1(in_35), .pin2(and_2_out), .pin3(AR1), .pin4(and_4_out), .pin5(AR3), .pin6(and_6_out),
    .pin7(n74240_1_pin7), .pin8(n74240_1_pin8), .pin9(n74240_1_pin9), .pin19(in_35), .pin18(AR0),
    .pin17(and_3_out), .pin16(AR2), .pin15(and_5_out), .pin14(AL), .pin13(n74240_1_pin13),
    .pin12(n74240_1_pin12), .pin11(n74240_1_pin11));
  and and_7 (and_7_out, n74138_2_pin15, n74138_2_pin14, n74138_2_pin13, n74138_2_pin12);
  and and_8 (and_8_out, n74138_2_pin9, n74138_2_pin7);
  not not_5 (not_5_out, n74138_1_pin9);
  _74161 #(.ShowInternalStructure("true")) u_74161_2 (
    .pin1(RST), .pin2(CLK1), .pin3(BUS4), .pin4(BUS5), .pin5(BUS6), .pin6(BUS7), .pin7(in_14),
    .pin15(n74161_2_pin15), .pin14(PC4), .pin13(PC5), .pin12(PC6), .pin11(PC7), .pin10(n74161_1_pin15),
    .pin9(PL));
  // NoConnect on n74240_1_pin13
  // NoConnect on n74240_1_pin7
  // NoConnect on n74240_1_pin8
  _74139 #(.ShowInternalStructure("true")) u_74139_2 (
    .pin1(IR4), .pin2(IR3), .pin3(IR2), .pin4(n74139_2_pin4));  // open: pin5, pin6, pin7, pin15, pin14, pin13, pin12, pin11, pin10, pin9
  or or_2 (OL, and_8_out, not_5_out);
  or or_3 (LD, and_7_out, not_5_out);
  // NoConnect on n74240_1_pin12
  // NoConnect on n74240_1_pin11
  // NoConnect on n74240_1_pin9
  not not_6 (not_6_out, WE);
  not not_7 (IX, n74138_2_pin7);
  not not_8 (not_8_out, OE);
  _74273 #(.ShowInternalStructure("true")) u_74273_1 (
    .pin1(in_15), .pin2(IR0), .pin3(ROM0), .pin4(ROM1), .pin5(IR1), .pin6(IR2), .pin7(ROM2), .pin8(ROM3),
    .pin9(IR3), .pin19(IR7), .pin18(ROM7), .pin17(ROM6), .pin16(IR6), .pin15(IR5), .pin14(ROM5),
    .pin13(ROM4), .pin12(IR4), .pin11(CLK1));
  _74273 #(.ShowInternalStructure("true")) u_74273_2 (
    .pin1(in_24), .pin2(D0), .pin3(ROM8), .pin4(ROM9), .pin5(D1), .pin6(D2), .pin7(ROM10), .pin8(ROM11),
    .pin9(D3), .pin19(D7), .pin18(ROM15), .pin17(ROM14), .pin16(D6), .pin15(D5), .pin14(ROM13),
    .pin13(ROM12), .pin12(D4), .pin11(CLK1));
  and and_9 (EH, n74138_2_pin13, n74138_2_pin12, n74138_2_pin7);
  and and_10 (EL, n74138_2_pin14, n74138_2_pin12, n74138_2_pin7);
  or or_4 (PH, n74139_2_pin4, n74138_1_pin7);
  RAM #(.addrWidth(15), .trigger("high")) ram_1 (
    .addr(n74157_2_pin9[14:0]), .we(not_6_out), .oe(not_8_out),
    .din({BUS7, BUS6, BUS5, BUS4, BUS3, BUS2, BUS1, BUS0}), .dout(ram_1_dout));
  _74153 #(.ShowInternalStructure("true")) u_74153_1 (
    .pin1(n74138_1_pin7), .pin2(CO), .pin3(in_29), .pin4(IR4), .pin5(IR3), .pin6(IR2), .pin7(n74153_1_pin7),
    .pin15(in_26), .pin14(AC7), .pin13(in_26), .pin12(in_26), .pin11(in_26), .pin10(in_26),
    .pin9(n74153_1_pin9));
  and and_11 (PL, not_9_out, PH);
  _74161 #(.ShowInternalStructure("true")) u_74161_3 (
    .pin1(RST), .pin2(CLK1), .pin3(Y0), .pin4(Y1), .pin5(Y2), .pin6(Y3), .pin7(PL), .pin15(n74161_3_pin15),
    .pin14(PC8), .pin13(PC9), .pin12(PC10), .pin11(PC11), .pin10(n74161_2_pin15), .pin9(PH));
  // NoConnect on n74153_1_pin9
  _74244 #(.ShowInternalStructure("true")) u_74244_1 (
    .pin1(DE), .pin2(D0), .pin3(BUS7), .pin4(D1), .pin5(BUS6), .pin6(D2), .pin7(BUS5), .pin8(D3),
    .pin9(BUS4), .pin19(DE), .pin18(BUS0), .pin17(D7), .pin16(BUS1), .pin15(D6), .pin14(BUS2), .pin13(D5),
    .pin12(BUS3), .pin11(D4));
  not not_9 (not_9_out, n74153_1_pin7);
  _74244 #(.ShowInternalStructure("true")) u_74244_2 (
    .pin1(OE), .pin2(ram_1_dout[0]), .pin3(BUS4), .pin4(ram_1_dout[1]), .pin5(BUS5), .pin6(ram_1_dout[2]),
    .pin7(BUS6), .pin8(ram_1_dout[3]), .pin9(BUS7), .pin19(OE), .pin18(BUS0), .pin17(ram_1_dout[4]),
    .pin16(BUS1), .pin15(ram_1_dout[5]), .pin14(BUS2), .pin13(ram_1_dout[6]), .pin12(BUS3),
    .pin11(ram_1_dout[7]));
  // NoConnect on n74161_4_pin15
  _74161 #(.ShowInternalStructure("true")) u_74161_4 (
    .pin1(RST), .pin2(CLK1), .pin3(Y4), .pin4(Y5), .pin5(Y6), .pin6(Y7), .pin7(PL), .pin15(n74161_4_pin15),
    .pin14(PC12), .pin13(PC13), .pin12(PC14), .pin11(PC15), .pin10(n74161_3_pin15), .pin9(PH));
  // Shift_Register shift_register_1: pin names not known; wires that end beside it: in_52, in_54, OUT6, in_58, in_56, in_56, in_56, in_56, in_56, in_56, in_56, in_56, in_53, shift_register_1_p14, shift_register_1_p15, shift_register_1_p16, shift_register_1_p17, shift_register_1_p18, shift_register_1_p19, shift_register_1_p20, shift_register_1_p21
  _74161 #(.ShowInternalStructure("true")) u_74161_5 (
    .pin1(OUT6), .pin2(CLK1), .pin7(in_36), .pin15(n74161_5_pin15), .pin14(n74161_5_pin14[0]),
    .pin13(n74161_5_pin14[1]), .pin12(n74161_5_pin14[2]), .pin11(n74161_5_pin14[3]), .pin10(in_36),
    .pin9(in_36));  // open: pin3, pin4, pin5, pin6
  _74161 #(.ShowInternalStructure("true")) u_74161_6 (
    .pin1(OUT7), .pin2(n74161_6_pin2), .pin7(in_36), .pin15(n74161_6_pin15), .pin14(n74161_6_pin14[0]),
    .pin13(n74161_6_pin14[1]), .pin12(n74161_6_pin14[2]), .pin11(n74161_6_pin14[3]), .pin10(in_36),
    .pin9(in_36));  // open: pin3, pin4, pin5, pin6
  not not_10 (n74161_6_pin2, OUT6);
  _74244 #(.ShowInternalStructure("true")) u_74244_3 (
    .pin1(IE), .pin2(shift_register_1_p14), .pin3(BUS4), .pin4(shift_register_1_p15), .pin5(BUS5),
    .pin6(shift_register_1_p16), .pin7(BUS6), .pin8(shift_register_1_p17), .pin9(BUS7), .pin19(IE),
    .pin18(BUS0), .pin17(shift_register_1_p18), .pin16(BUS1), .pin15(shift_register_1_p19), .pin14(BUS2),
    .pin13(shift_register_1_p20), .pin12(BUS3), .pin11(shift_register_1_p21));
  _74377 #(.ShowInternalStructure("true")) u_74377_1 (
    .pin1(LD), .pin2(AC3), .pin3(ALU3), .pin4(ALU2), .pin5(AC2), .pin6(AC1), .pin7(ALU1), .pin8(ALU0),
    .pin9(AC0), .pin19(AC6), .pin18(ALU6), .pin17(ALU7), .pin16(AC7), .pin15(AC4), .pin14(ALU4),
    .pin13(ALU5), .pin12(AC5), .pin11(CLK2));
  _74244 #(.ShowInternalStructure("true")) u_74244_4 (
    .pin1(AE), .pin2(AC0), .pin3(BUS7), .pin4(AC1), .pin5(BUS6), .pin6(AC2), .pin7(BUS5), .pin8(AC3),
    .pin9(BUS4), .pin19(AE), .pin18(BUS0), .pin17(AC7), .pin16(BUS1), .pin15(AC6), .pin14(BUS2), .pin13(AC5),
    .pin12(BUS3), .pin11(AC4));
  _74161 #(.ShowInternalStructure("true")) u_74161_7 (
    .pin1(OUT6), .pin2(CLK1), .pin7(in_37), .pin14(n74161_5_pin14[4]), .pin13(n74161_5_pin14[5]),
    .pin12(n74161_5_pin14[6]), .pin11(n74161_5_pin14[7]), .pin10(n74161_5_pin15), .pin9(in_37));  // open: pin3, pin4, pin5, pin6, pin15
  _74161 #(.ShowInternalStructure("true")) u_74161_8 (
    .pin1(OUT7), .pin2(n74161_6_pin2), .pin7(in_37), .pin14(n74161_6_pin14[4]), .pin13(n74161_6_pin14[5]),
    .pin12(n74161_6_pin14[6]), .pin11(n74161_6_pin14[7]), .pin10(n74161_6_pin15), .pin9(in_37));  // open: pin3, pin4, pin5, pin6, pin15
  _74153 #(.ShowInternalStructure("true")) u_74153_2 (
    .pin1(in_9), .pin2(BUS3), .pin3(AR3), .pin4(AR2), .pin5(AR1), .pin6(AR0), .pin7(n74153_2_pin7),
    .pin15(AL), .pin14(AC3), .pin13(in_1), .pin12(in_5), .pin11(in_1), .pin10(in_5), .pin9(n74153_2_pin9));
  _74153 #(.ShowInternalStructure("true")) u_74153_3 (
    .pin1(AL), .pin2(AC4), .pin3(in_16), .pin4(in_16), .pin5(in_20), .pin6(in_20), .pin7(n74153_3_pin7),
    .pin15(in_20), .pin14(BUS4), .pin13(AR3), .pin12(AR1), .pin11(AR2), .pin10(AR0), .pin9(n74153_3_pin9));
  and and_12 (and_12_out, OUT6, OUT7);
  not not_11 (not_11_out, RST);
  _74153 #(.ShowInternalStructure("true")) u_74153_4 (
    .pin1(in_10), .pin2(BUS2), .pin3(AR3), .pin4(AR2), .pin5(AR1), .pin6(AR0), .pin7(n74153_4_pin7),
    .pin15(AL), .pin14(AC2), .pin13(in_2), .pin12(in_6), .pin11(in_2), .pin10(in_6), .pin9(n74153_4_pin9));
  _74153 #(.ShowInternalStructure("true")) u_74153_5 (
    .pin1(AL), .pin2(AC5), .pin3(in_17), .pin4(in_17), .pin5(in_21), .pin6(in_21), .pin7(n74153_5_pin7),
    .pin15(in_21), .pin14(BUS5), .pin13(AR3), .pin12(AR1), .pin11(AR2), .pin10(AR0), .pin9(n74153_5_pin9));
  // RGB_Video #(.height(256), .width(256)) rgb_video_1: pin names not known; wires that end beside it: not_11_out, CLK1, and_12_out, n74161_5_pin14, n74161_6_pin14, {OUT5, OUT4, OUT5, OUT4, OUT5, OUT4, OUT5, OUT4, OUT3, OUT2, OUT3, OUT2, OUT3, OUT2, OUT3, OUT2, OUT1, OUT0, OUT1, OUT0, OUT1, OUT0, OUT1, OUT0}
  _74161 #(.ShowInternalStructure("true")) u_74161_9 (
    .pin1(in_25), .pin2(CLK2), .pin3(ALU4), .pin4(ALU5), .pin5(ALU6), .pin6(ALU7), .pin7(IX), .pin14(X4),
    .pin13(X5), .pin12(X6), .pin11(X7), .pin10(n74161_9_pin10), .pin9(XL));  // open: pin15
  _74161 #(.ShowInternalStructure("true")) u_74161_10 (
    .pin1(in_30), .pin2(CLK2), .pin3(ALU0), .pin4(ALU1), .pin5(ALU2), .pin6(ALU3), .pin7(IX),
    .pin15(n74161_9_pin10), .pin14(X0), .pin13(X1), .pin12(X2), .pin11(X3), .pin10(in_28), .pin9(XL));
  _74153 #(.ShowInternalStructure("true")) u_74153_6 (
    .pin1(in_11), .pin2(BUS1), .pin3(AR3), .pin4(AR2), .pin5(AR1), .pin6(AR0), .pin7(n74153_6_pin7),
    .pin15(AL), .pin14(AC1), .pin13(in_3), .pin12(in_7), .pin11(in_3), .pin10(in_7), .pin9(n74153_6_pin9));
  _74153 #(.ShowInternalStructure("true")) u_74153_7 (
    .pin1(AL), .pin2(AC6), .pin3(in_18), .pin4(in_18), .pin5(in_22), .pin6(in_22), .pin7(n74153_7_pin7),
    .pin15(in_22), .pin14(BUS6), .pin13(AR3), .pin12(AR1), .pin11(AR2), .pin10(AR0), .pin9(n74153_7_pin9));
  _74153 #(.ShowInternalStructure("true")) u_74153_8 (
    .pin1(in_12), .pin2(BUS0), .pin3(AR3), .pin4(AR2), .pin5(AR1), .pin6(AR0), .pin7(n74153_8_pin7),
    .pin15(AL), .pin14(AC0), .pin13(in_4), .pin12(in_8), .pin11(in_4), .pin10(in_8), .pin9(n74153_8_pin9));
  _74153 #(.ShowInternalStructure("true")) u_74153_9 (
    .pin1(AL), .pin2(AC7), .pin3(in_19), .pin4(in_19), .pin5(in_23), .pin6(in_23), .pin7(n74153_9_pin7),
    .pin15(in_23), .pin14(BUS7), .pin13(AR3), .pin12(AR1), .pin11(AR2), .pin10(AR0), .pin9(n74153_9_pin9));
  _74377 #(.ShowInternalStructure("true")) u_74377_2 (
    .pin1(YL), .pin2(Y0), .pin3(ALU0), .pin4(ALU1), .pin5(Y1), .pin6(Y2), .pin7(ALU2), .pin8(ALU3),
    .pin9(Y3), .pin19(Y4), .pin18(ALU4), .pin17(ALU5), .pin16(Y5), .pin15(Y6), .pin14(ALU6), .pin13(ALU7),
    .pin12(Y7), .pin11(CLK2));
  Hex_Digit_Display hex_digit_display_1 (.value({in_74, in_71, in_65, BUS7}));  // open: dp
  Hex_Digit_Display hex_digit_display_2 (.value({in_98, in_95, in_90, PC7}));  // open: dp
  Hex_Digit_Display hex_digit_display_3 (.value({in_110, in_109, in_107, OUT7}));  // open: dp
  Hex_Digit_Display hex_digit_display_4 (.value({in_110, in_109, in_107, OUT6}));  // open: dp
  Hex_Digit_Display hex_digit_display_5 (.value({in_74, in_71, in_65, BUS6}));  // open: dp
  Hex_Digit_Display hex_digit_display_6 (.value({in_74, in_71, in_65, BUS5}));  // open: dp
  Hex_Digit_Display hex_digit_display_7 (.value({in_98, in_95, in_90, PC6}));  // open: dp
  Hex_Digit_Display hex_digit_display_8 (.value({in_98, in_95, in_90, PC5}));  // open: dp
  Hex_Digit_Display hex_digit_display_9 (.value({in_110, in_109, in_107, OUT5}));  // open: dp
  Hex_Digit_Display hex_digit_display_10 (.value({in_110, in_109, in_107, OUT4}));  // open: dp
  _74283 #(.ShowInternalStructure("true")) u_74283_1 (
    .pin1(ALU1), .pin2(n74153_6_pin9), .pin3(n74153_6_pin7), .pin4(ALU0), .pin5(n74153_8_pin7),
    .pin6(n74153_8_pin9), .pin7(AR0), .pin15(n74153_4_pin9), .pin14(n74153_4_pin7), .pin13(ALU2),
    .pin12(n74153_2_pin7), .pin11(n74153_2_pin9), .pin10(ALU3), .pin9(n74283_1_pin9));
  _74283 #(.ShowInternalStructure("true")) u_74283_2 (
    .pin1(ALU5), .pin2(n74153_5_pin7), .pin3(n74153_5_pin9), .pin4(ALU4), .pin5(n74153_3_pin7),
    .pin6(n74153_3_pin9), .pin7(n74283_1_pin9), .pin15(n74153_7_pin7), .pin14(n74153_7_pin9), .pin13(ALU6),
    .pin12(n74153_9_pin7), .pin11(n74153_9_pin9), .pin10(ALU7), .pin9(CO));
  Counter counter_1 (.clk(in_34));  // open: clr, load, up, count, D, carry, Q
  Hex_Digit_Display hex_digit_display_11 (.value({ROM15, ROM14, ROM13, ROM12}));  // open: dp
  Hex_Digit_Display hex_digit_display_12 (.value({in_74, in_71, in_65, BUS4}));  // open: dp
  Hex_Digit_Display hex_digit_display_13 (.value({in_66, in_62, in_59, BUS3}));  // open: dp
  Hex_Digit_Display hex_digit_display_14 (.value({in_98, in_95, in_90, PC4}));  // open: dp
  Hex_Digit_Display hex_digit_display_15 (.value({in_91, in_86, in_83, PC3}));  // open: dp
  Hex_Digit_Display hex_digit_display_16 (.value({in_108, in_106, in_105, OUT3}));  // open: dp
  Hex_Digit_Display hex_digit_display_17 (.value({in_108, in_106, in_105, OUT2}));  // open: dp
  Hex_Digit_Display hex_digit_display_18 (.value({ROM11, ROM10, ROM9, ROM8}));  // open: dp
  Hex_Digit_Display hex_digit_display_19 (.value({ROM7, ROM6, ROM5, ROM4}));  // open: dp
  Hex_Digit_Display hex_digit_display_20 (.value({in_66, in_62, in_59, BUS2}));  // open: dp
  Hex_Digit_Display hex_digit_display_21 (.value({in_66, in_62, in_59, BUS1}));  // open: dp
  Hex_Digit_Display hex_digit_display_22 (.value({in_91, in_86, in_83, PC2}));  // open: dp
  Hex_Digit_Display hex_digit_display_23 (.value({in_91, in_86, in_83, PC1}));  // open: dp
  Hex_Digit_Display hex_digit_display_24 (.value({in_108, in_106, in_105, OUT1}));  // open: dp
  Hex_Digit_Display hex_digit_display_25 (.value({in_108, in_106, in_105, OUT0}));  // open: dp
  Hex_Digit_Display hex_digit_display_26 (.value({ROM3, ROM2, ROM1, ROM0}));  // open: dp
  Hex_Digit_Display hex_digit_display_27 (.value({in_66, in_62, in_59, BUS0}));  // open: dp
  Hex_Digit_Display hex_digit_display_28 (.value({in_91, in_86, in_83, PC0}));  // open: dp
  Hex_Digit_Display hex_digit_display_29 (.value({in_48, in_46, in_42, ROM7}));  // open: dp
  Hex_Digit_Display hex_digit_display_30 (.value({in_48, in_46, in_42, ROM6}));  // open: dp
  Hex_Digit_Display hex_digit_display_31 (.value({in_48, in_46, in_42, ROM5}));  // open: dp
  Hex_Digit_Display hex_digit_display_32 (.value({in_48, in_46, in_42, ROM4}));  // open: dp
  Hex_Digit_Display hex_digit_display_33 (.value({in_75, in_72, in_67, ALU7}));  // open: dp
  Hex_Digit_Display hex_digit_display_34 (.value({in_96, in_92, in_87, X7}));  // open: dp
  _74377 #(.ShowInternalStructure("true")) u_74377_3 (
    .pin1(OL), .pin2(OUT3), .pin3(ALU3), .pin4(ALU2), .pin5(OUT2), .pin6(OUT1), .pin7(ALU1), .pin8(ALU0),
    .pin9(OUT0), .pin19(OUT7), .pin18(ALU7), .pin17(ALU6), .pin16(OUT6), .pin15(OUT5), .pin14(ALU5),
    .pin13(ALU4), .pin12(OUT4), .pin11(CLK2));
  Hex_Digit_Display hex_digit_display_35 (.value({in_43, in_40, in_38, ROM3}));  // open: dp
  Hex_Digit_Display hex_digit_display_36 (.value({in_43, in_40, in_38, ROM2}));  // open: dp
  Hex_Digit_Display hex_digit_display_37 (.value({in_75, in_72, in_67, ALU6}));  // open: dp
  Hex_Digit_Display hex_digit_display_38 (.value({in_75, in_72, in_67, ALU5}));  // open: dp
  Hex_Digit_Display hex_digit_display_39 (.value({in_96, in_92, in_87, X6}));  // open: dp
  Hex_Digit_Display hex_digit_display_40 (.value({in_96, in_92, in_87, X5}));  // open: dp
  Hex_Digit_Display hex_digit_display_41 (.value({in_43, in_40, in_38, ROM1}));  // open: dp
  Hex_Digit_Display hex_digit_display_42 (.value({in_43, in_40, in_38, ROM0}));  // open: dp
  Hex_Digit_Display hex_digit_display_43 (.value({in_75, in_72, in_67, ALU4}));  // open: dp
  Hex_Digit_Display hex_digit_display_44 (.value({in_68, in_63, in_60, ALU3}));  // open: dp
  Hex_Digit_Display hex_digit_display_45 (.value({in_96, in_92, in_87, X4}));  // open: dp
  Hex_Digit_Display hex_digit_display_46 (.value({in_88, in_84, in_82, X3}));  // open: dp
  Hex_Digit_Display hex_digit_display_47 (.value({in_68, in_63, in_60, ALU2}));  // open: dp
  Hex_Digit_Display hex_digit_display_48 (.value({in_68, in_63, in_60, ALU1}));  // open: dp
  Hex_Digit_Display hex_digit_display_49 (.value({in_88, in_84, in_82, X2}));  // open: dp
  Hex_Digit_Display hex_digit_display_50 (.value({in_88, in_84, in_82, X1}));  // open: dp
  Hex_Digit_Display hex_digit_display_51 (.value({in_68, in_63, in_60, ALU0}));  // open: dp
  Hex_Digit_Display hex_digit_display_52 (.value({in_88, in_84, in_82, X0}));  // open: dp
  Hex_Digit_Display hex_digit_display_53 (.value({in_49, in_47, in_44, ROM15}));  // open: dp
  Hex_Digit_Display hex_digit_display_54 (.value({in_49, in_47, in_44, ROM14}));  // open: dp
  Hex_Digit_Display hex_digit_display_55 (.value({in_49, in_47, in_44, ROM13}));  // open: dp
  Hex_Digit_Display hex_digit_display_56 (.value({in_49, in_47, in_44, ROM12}));  // open: dp
  Hex_Digit_Display hex_digit_display_57 (.value({in_76, in_73, in_69, AC7}));  // open: dp
  Hex_Digit_Display hex_digit_display_58 (.value({in_45, in_41, in_39, ROM11}));  // open: dp
  Hex_Digit_Display hex_digit_display_59 (.value({in_45, in_41, in_39, ROM10}));  // open: dp
  Hex_Digit_Display hex_digit_display_60 (.value({in_76, in_73, in_69, AC6}));  // open: dp
  Hex_Digit_Display hex_digit_display_61 (.value({in_76, in_73, in_69, AC5}));  // open: dp
  Hex_Digit_Display hex_digit_display_62 (.value({in_99, in_97, in_93, Y7}));  // open: dp
  Hex_Digit_Display hex_digit_display_63 (.value({in_99, in_97, in_93, Y6}));  // open: dp
  Hex_Digit_Display hex_digit_display_64 (.value({in_45, in_41, in_39, ROM9}));  // open: dp
  Hex_Digit_Display hex_digit_display_65 (.value({in_45, in_41, in_39, ROM8}));  // open: dp
  Hex_Digit_Display hex_digit_display_66 (.value({in_76, in_73, in_69, AC4}));  // open: dp
  Hex_Digit_Display hex_digit_display_67 (.value({in_70, in_64, in_61, AC3}));  // open: dp
  Hex_Digit_Display hex_digit_display_68 (.value({in_99, in_97, in_93, Y5}));  // open: dp
  Hex_Digit_Display hex_digit_display_69 (.value({in_99, in_97, in_93, Y4}));  // open: dp
  Hex_Digit_Display hex_digit_display_70 (.value({in_70, in_64, in_61, AC2}));  // open: dp
  Hex_Digit_Display hex_digit_display_71 (.value({in_70, in_64, in_61, AC1}));  // open: dp
  Hex_Digit_Display hex_digit_display_72 (.value({in_94, in_89, in_85, Y3}));  // open: dp
  Hex_Digit_Display hex_digit_display_73 (.value({in_94, in_89, in_85, Y2}));  // open: dp
  Hex_Digit_Display hex_digit_display_74 (.value({in_70, in_64, in_61, AC0}));  // open: dp
  Hex_Digit_Display hex_digit_display_75 (.value({in_94, in_89, in_85, Y1}));  // open: dp
  Hex_Digit_Display hex_digit_display_76 (.value({in_94, in_89, in_85, Y0}));  // open: dp

  // Other names for the same wires on the sheet: hand = in_34; SER_DATA = in_58; SER_LATCH = in_57; SER_PULSE = in_55

  // Notes on the sheet:
  //   in_14: initial=0x1
  //   in_24: initial=0x1
  //   in_15: initial=0x1
  //   in_26: initial=0x1
  //   in_33: initial=0x1
  //   in_54: initial=0x1
  //   in_77: initial=0x1
  //   in_78: initial=0x1
  //   in_79: initial=0x1
  //   in_80: initial=0x1
  //   in_100: initial=0x1
  //   in_101: initial=0x1
  //   in_102: initial=0x1
  //   in_103: initial=0x1
  //   in_36: initial=0x1
  //   in_16: initial=0x1
  //   in_37: initial=0x1
  //   in_1: initial=0x1
  //   in_55: initial=0x1
  //   in_57: initial=0x1
  //   in_58: initial=0x1
  //   in_17: initial=0x1
  //   in_2: initial=0x1
  //   in_25: initial=0x1
  //   in_30: initial=0x1
  //   in_28: initial=0x1
  //   in_18: initial=0x1
  //   in_3: initial=0x1
  //   in_19: initial=0x1
  //   in_4: initial=0x1
  //   in_13: initial=0x1
  //   RAM
  //   命令デコーダ
  //   BUS_ACCESS_DECODER
  //   MODE_DECODER
  //   INSTRUCTION_DECODER
  //   クロック回路
  //   リセット回路
  //   ROM
  //   プログラムカウンタ
  //   contents of rom_1 (hex, n*v repeats v):
  //   0 8018 c018 7fc1 7cc1 100 1d6 ff00 69 ca c2 69 cec ff00 69 ca 61 15f0 101 6fc 82 ff00 c2 17ec 1a0 1
  //   16ec 1a0 100 8018 c018 0 18d2 19d6 601 26f4 8d bf60 6c2 701 2bf4 681 c160 7c2 881 8c2 1801 180 22ec
  //   18d2 1901 180 22ec 19d6 300 8018 c018 ee00 16c2 290 100 17d6 59dc 5fdc 2bdc 22dc b4dc e2dc dc dc
  //   fcdc dc 200 5c2 ff00 ec2 fc2 10c2 11c2 12c2 700 8018 c018 0 c2 2c2 2cc2 f00 8018 c018 13c2 14c2 114
  //   3e0 2ec2 4800 21c2 0 1cc2 114 f9ca f6ca f7ca 2cc2 1ac2 200 1bc2 f600 ac2 bc2 cc2 ad00 22c2 bd00 24c2
  //   f300 25c2 1601 2a0 16c2 7fc1 7cc1 1d01 314 cbe0 e800 2 2 314 cbe0 f600 314 cbe0 f600 314 cbe0 f600
  //   314 cbe0 f600 314 cbe0 f600 314 cbe0 f600 314 cbe0 f600 314 cbe0 f600 314 cbe0 f600 314 cbe0 f600
  //   1414 5ce0 2a01 1414 94e0 2801 314 cbe0 f600 314 cbe0 f600 314 cbe0 f600 1214 42e0 0 314 cbe0 f600
  //   314 cbe0 f600 314 cbe0 f600 314 cbe0 f600 314 cbe0 f600 314 cbe0 f600 314 cbe0 f600 314 cbe0 f600
  //   314 cbe0 f600 314 cbe0 f600 314 cbe0 f600 314 cbe0 f600 314 cbe0 f600 314 cbe0 f600 314 cbe0 f600
  //   314 cbe0 f600 314 cbe0 f600 1414 27e0 1901 1414 e0 2515 1314 e0 1801 1314 78e0 1901 f714 6ce0 1901 2
  //   2 2419 2 314 cbe0 f500 18c3 0 19c2 2 314 cbe0 f400 515 ffe0 7f00 c000 1fc2 8000 20c2 b300 9c2 100
  //   80c2 e81 ec2 761 f61 681 6c2 881 8c2 16e8 17fc 5360 6c60 781 7c2 2d01 1df0 1efc 1a0 2f01 2dc2 22f0
  //   23fc 0 100 2e81 27ec 28fc e800 2ce4 2ec2 4880 fe 48fc f00 2ec2 48fc 1421 f00 700 300 100 200 400 800
  //   400 200 100 300 700 f00 e00 c00 800 400 200 100 200 400 800 c00 e00 14c2 1000 dc2 e01 52f0 5500 1ec2
  //   515 ffe0 2300 1214 e0 114 2101 fb20 21c2 2c01 5cec 5dfc 0 f000 1441 14c2 2c01 63f0 64fc 1a0 0 2cc2
  //   1f19 201 2121 180 2019 2d6 7f00 fe29 fc89 feca 8030 5 ff89 fd89 ffca fc20 fb69 12 fa09 714 8d 7de8
  //   7efc 3f20 3f00 381 3c2 1301 1214 1f19 901 b1f4 280 9c2 bda0 8dec da1 4000 92fc 1fc2 91ec c000 93fc
  //   1fc2 1f01 2 4060 20c2 901 cf60 9aec 9bfc fc3 c0 901 620 a6f0 301 a400 1ec2 515 ffe0 3500 66fc 1f19
  //   f40 1421 13c2 3c0 af00 1ec2 515 ffe0 3300 66fc 1f19 25e0 114 1101 ef60 beec 1201 1a0 12c2 7f20 c6f0
  //   ee00 c5fc c4fc 100 bfec 1a0 2 8000 12c2 cbfc 2 16c2 100 17c2 200 5c2 1101 df60 e2ec b01 d5e8 a01 bc2
  //   c01 ac2 dafc f600 a00 bc2 ac2 2 cc2 3500 dcec 1a0 2 11c2 eafc 0 201 320 2c2 ea00 1ec2 515 ffe0 2600
  //   114 f909 9c2 1fc2 f1ec f2fc 100 ec00 dc2 201 2121 180 214 b1e0 8018 6*2 aefc 201 ca00 dc2 114 911 d
  //   de 20c2 d 1f91 2015 c000 160*5d c018 201 2121 180 8018 2d6 7f00 fe29 fc89 feca 8030 5 ff89 fd89 ffca
  //   fc20 fb69 12 fa09 714 8d c4e8 c5fc 3f20 3f00 381 3c2 1301 dfd c018 d300 dc2 114 901 190 1f01 8d afd
  //   1fd2 dc00 dc2 301 f40 1421 13c2 3c0 bfd 1f11 1f11 901 eea0 e5f0 f080 9c2 100 cfd dc2 3c0 e900 cfd
  //   dc2 114 4e0 c000 2001 8080 20d2 1f01 a5 f4f0 1fc2 f6fc 100 dc2 ff00 1ec2 515 ffe0 3c00 4*2 3fc 1715
  //   1581 be8 15c2 1601 280 16d2 d de fe d e80 ce4 1a0 114 1ee1 0 18c2 de d 19c2 1601 180 16c2 f600 1fc
  //   12 5 414 13e0 18c2 b14 d2e0 12 180 1dc2 5 18c2 1d11 5 19c2 1fc f600 12 180 1dc2 1801 c6 1d11 1901 c6
  //   1fc f600 1901 40ec 1dc2 1801 43f0 100 1dc2 d fe 1d01 45ec 48f0 d 2 3dfc d 1601 4afc 180 de d 16c2
  //   1fc f200 45f8 48e4 d 45f4 48e8 d 45e8 48f4 d 45e4 48f8 d 18c2 0 19c2 fc f800 12 1801 c6 fc f800 1c11
  //   5 1ac2 1c01 190 5 1bc2 1c01 280 1cc2 1601 1a0 16c2 fc f300 45f0 48ec d 1c01 1b0 1b01 c6 1c01 2a0
  //   1cd2 1a01 6dfc c6 1915 fbe0 1881 414 11e0 1821 b14 c6e0 1601 1841 18c2 1fc f900 1861 18c2 1fc f900
  //   16c2 fc f900 12 414 e4e0 100 b14 dee0 12 180 1dc2 1801 85 18c2 a3e8 a5 a5fc 45 25 2 8030 5 1981 1d11
  //   85 19c2 1fc f200 414 62e0 1601 2a0 16c2 cbfc f600 1581 afe8 2315 22e1 12 180 1dc2 1801 c1e8 a5 18c2
  //   c4fc 45 18c2 25 2 8030 1901 a5 1d11 a5 19c2 f200 1fc 1715 414 7e0 1dc2 1601 280 1ac2 1701 1bc2 1d11
  //   5 2a0 16c2 1d01 190 5 17d6 1fc f300 1c81 1cc2 1fc f900 414 18e0 1dc2 414 26e0 1dc2 414 35e0 1801 414
  //   41e0 414 4ce0 414 57e0 1dc2 414 6de0 1dc2 414 7ae0 414 86e0 414 91e0 414 9ce0 1dc2 1a01 2a0 16c2
  //   1b01 17c2 314 cbe0 f600 1601 280 18c2 1701 19c2 1d01 16c2 314 e0 f400 2 18c2 0 19c2 314 cbe0 f500
  //   1881 18c2 1ee8 1da1 20fc 1d41 1d21 2 8030 5 1981 314 cae0 19c2 1801 2ce8 1da1 18c2 2ffc 1d41 18c2
  //   1d21 2 8030 1901 a5 314 c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
  //   5
  //   7
  //   2
  //   3
  //   5
  //   AR0
  //   AR1
  //   AR2
  //   AR3
  //   AL
  //   0
  //   1
  //   2
  //   3
  //   6
  //   7
  //   To RAM
  //   6
  //   7
  //   2
  //   3
  //   7
  //   1
  //   3
  //   7
  //   IR2
  //   IR3
  //   IR4
  //   5
  //   4
  //   To ALU
  //   InstructionRegister
  //   DataRegister
  //   To User Registers
  //   To memory address unit
  //   To user registeres
  //   To program counter
  //   I/O
  //   ALU
  //   Register
  //   Bus gateway AC
  //   Accumlator
  //   X register
  //   Out
  //   Debug
  //   ROM
  //   BUS
  //   PC
  //   Y register
  //   COUNT
  //   IR
  //   ALU
  //   X register
  //   Output register
  //   D
  //   AC
  //   Y register
endmodule
